# Fritzing sketch Humaniod Robot Connection Diagram (saved by Fritzing 0.9.3b)

parts:
  Part1 = Arduino Nano (Rev3.0)
  Part2 = Adafruit PCA9685 PWM/Servo Breakout [part_number=815]
  M1 = Dagu DGServo 9g (Top view) [part_number=RS001B]
  M2 = Dagu DGServo 9g (Top view) [part_number=RS001B]
  M3 = Dagu DGServo 9g (Top view) [part_number=RS001B]  # not connected
  M4 = Dagu DGServo 9g (Top view) [part_number=RS001B]
  M5 = Dagu DGServo 9g (Top view) [part_number=RS001B]
  M6 = Dagu DGServo 9g (Top view) [part_number=RS001B]
  M7 = Dagu DGServo 9g (Top view) [part_number=RS001B]
  M8 = Dagu DGServo 9g (Top view) [part_number=RS001B]  # not connected
  M9 = Dagu DGServo 9g (Top view) [part_number=RS001B]
  M11 = Dagu DGServo 9g (Top view) [part_number=RS001B]
  M12 = Dagu DGServo 9g (Top view) [part_number=RS001B]
  M13 = Dagu DGServo 9g (Top view) [part_number=RS001B]
  M14 = Dagu DGServo 9g (Top view) [part_number=RS001B]
  M15 = Dagu DGServo 9g (Top view) [part_number=RS001B]
  M16 = Dagu DGServo 9g (Top view) [part_number=RS001B]
  M17 = Dagu DGServo 9g (Top view) [part_number=RS001B]
  M18 = Dagu DGServo 9g (Top view) [part_number=RS001B]
  M10 = Dagu DGServo 9g (Top view) [part_number=RS001B]
  5V-6V = 2.1mm Barrel Jack with Terminal Block
  5V-12V = 2.1mm Barrel Jack with Terminal Block
  Part3 = Bluetooth HC-05 Macho
  LED2 = LEDs [package=led10mm]
  LED3 = LEDs [package=led10mm]

nets:
  N1: Part1.D1/TX, Part3.RXD
  N2: Part1.D0/RX, Part3.TXD
  N3: Part1.GND, 5V-12V.NEG
  N4: Part1.D6, LED3.C
  N5: Part1.D8, LED2.C
  N6: Part1.VIN, 5V-12V.POS
  5V: Part1.5V, Part2.VCC
  N7: Part1.A5, Part2.SCL
  N8: Part1.A4, Part2.SDA
  N9: Part2.PWRIN, 5V-6V.POS
  GND: Part2.GND, M9.gnd, 5V-6V.NEG
  N10: Part2.PWM7, M12.pulse
  N11: Part2.PWM6, M15.pulse
  N12: Part2.PWM5, M17.pulse
  N13: Part2.PWM4, M18.pulse
  N14: Part2.PWM3, M6.pulse
  N15: Part2.PWM2, M4.pulse
  N16: Part2.PWM1, M2.pulse
  N17: Part2.PWM0, M1.pulse
  N18: Part2.PWM15, M10.pulse
  N19: Part2.PWM14, M9.pulse
  N20: Part2.PWM13, M7.pulse
  N21: Part2.PWM12, M5.pulse
  N22: Part2.PWM11, M13.pulse
  N23: Part2.PWM10, M16.pulse
  N24: Part2.PWM9, M14.pulse
  N25: Part2.PWM8, M11.pulse
  N26: LED2.A, LED3.A

custom parts:
  Adafruit PCA9685 PWM/Servo Breakout: Using only two pins, control 16 free-running PWM outputs! I2C-controlled PWM driver with a built in clock. Unlike the TLC5940 family, you do not need to continuously send it signal tying up your microcontroller, its completely free running! 5V compliant, which means you can control it from a 3.3V microcontroller and still safely drive up to 6V outputs (this is good for when you want to control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
